// Logisim project fsm_pass_check.circ as structural Verilog: 1 circuit, main circuit main
module main (
  input  S3,
  input  S2,
  input  S1,
  input  S0
);

  wire and_1_out, and_2_out, and_3_out, and_4_out, button_1_out, button_2_out, d_ff_1_q, d_ff_1_qn, d_ff_2_q,
       d_ff_3_q, d_ff_3_qn, Green_out, not_1_out, not_2_out, not_3_out, not_4_out, or_1_out, or_2_out,
       or_3_out, Red_out;

  or or_1 (or_1_out, and_4_out, and_1_out);
  and and_1 (and_1_out, not_3_out, d_ff_1_qn);
  Button button_1 (.out(button_1_out));
  not not_1 (not_1_out, S2);
  not not_2 (not_2_out, S1);
  and and_2 (and_2_out, S3, not_1_out, not_2_out, S0);
  not not_3 (not_3_out, and_2_out);
  D_Flip_Flop d_ff_1 (
    .clk(button_1_out), .D(or_1_out), .Q(d_ff_1_q), .Qn(d_ff_1_qn), .en(1'b1), .reset(button_2_out));  // open: preset
  Button button_2 (.out(button_2_out));
  and and_3 (and_3_out, not_3_out, or_3_out);
  or or_2 (or_2_out, and_4_out, and_3_out);
  D_Flip_Flop d_ff_2 (
    .clk(button_1_out), .D(or_2_out), .Q(d_ff_2_q), .en(1'b1), .reset(button_2_out));  // open: Qn, preset
  D_Flip_Flop d_ff_3 (
    .clk(button_1_out), .D(and_2_out), .Q(d_ff_3_q), .Qn(d_ff_3_qn), .en(1'b1), .reset(button_2_out));  // open: preset
  or or_3 (or_3_out, d_ff_2_q, d_ff_1_q);
  and and_4 (and_4_out, d_ff_1_q, d_ff_2_q);
  LED led_1 (.in(and_4_out));
  not not_4 (not_4_out, and_4_out);
  LED led_2 (.in(Green_out));
  and Green (Green_out, not_4_out, d_ff_3_q);
  LED led_3 (.in(Red_out));
  and Red (Red_out, not_4_out, d_ff_3_qn);

  // Notes on the sheet:
  //   Match: S3.S2'.S1'.S0
  //   Wrong: Match'
  //   Match 
  //   Clock
  //   D0
  //   Reset
  //   Wrong
  //   D1
  //   D0 = (wrong.Q0') + Q0.Q1
  //   Outputs For Led:
  //   Yellow(LOCK): Q1.Q0
  //   not lock = (Q1.Q0)'
  //   Inputs and Outputs for D Flip Flips
  //   D1 = wrong.(Q1+Q0) + Q0.Q1
  //   D = Match, Output = stored match
  //   Green(MATCH): stored match and not lock
  //   Red(WRONG): stored wrong and not lock
  //   stored match
  //   store wrong
endmodule
